// Logisim project DL.1.circ as structural Verilog: 1 circuit, main circuit main
module main (
  input  in_1,
  input  Y,
  input  in_3,
  input  in_4,
  input  Y_2,
  input  in_6,
  input  in_7,
  input  Y_3,
  input  in_9,
  input  Y_4,
  input  in_11,
  input  in_12,
  input  Y_5,
  input  in_14
);

  wire and_1_out, not_1_out, or_1_out, xnor_1_out, xor_1_out;

  and and_1 (and_1_out, in_1, in_3);
  or or_1 (or_1_out, in_4, in_6);
  not not_1 (not_1_out, in_7);
  xor xor_1 (xor_1_out, in_9, in_11);
  xnor xnor_1 (xnor_1_out, in_12, in_14);
endmodule
